// Logisim project 4-BitAdder.circ as structural Verilog: 2 circuits, main circuit Ripple Adder
module Full_Adder (
  input  Cin,
  input  A,
  input  B,
  output S,
  output Cout
);

  wire and_1_out, and_2_out, xor_1_out;

  xor xor_1 (xor_1_out, A, B);
  and and_1 (and_1_out, A, B);
  xor xor_2 (S, xor_1_out, Cin);
  and and_2 (and_2_out, Cin, xor_1_out);
  or or_1 (Cout, and_2_out, and_1_out);
endmodule

module Ripple_Adder (
  input  Selector,
  input  [3:0] B,
  input  [3:0] A,
  output [3:0] sum,
  output Carry,
  output Overflow,
  output Sign,
  output Zero
);

  wire full_adder_1_cout, full_adder_2_cout, full_adder_3_cout, xor_1_out, xor_2_out, xor_3_out, xor_4_out;

  xor xor_1 (xor_1_out, Selector, B[0]);
  xor xor_2 (xor_2_out, Selector, B[1]);
  xor xor_3 (xor_3_out, Selector, B[2]);
  xor xor_4 (xor_4_out, Selector, B[3]);
  Full_Adder full_adder_1 (.Cin(Selector), .A(A[0]), .B(xor_1_out), .S(sum[0]), .Cout(full_adder_1_cout));
  Full_Adder full_adder_2 (.Cin(full_adder_1_cout), .A(A[1]), .B(xor_2_out), .S(sum[1]), .Cout(full_adder_2_cout));
  Full_Adder full_adder_3 (.Cin(full_adder_2_cout), .A(A[2]), .B(xor_3_out), .S(sum[2]), .Cout(full_adder_3_cout));
  Full_Adder full_adder_4 (.Cin(full_adder_3_cout), .A(A[3]), .B(xor_4_out), .S(sum[3]), .Cout(Carry));
  xor xor_5 (Overflow, Carry, Selector);
  and and_1 (Sign, sum[3], Selector);
  nor nor_1 (Zero, sum[3], sum[2], sum[1], sum[0]);
endmodule
